# Fritzing sketch 1v25-dc-dc (saved by Fritzing 0.9.3b)
circuit board: 8.59112cm x 5.458cm
breadboards: 1

parts:
  U1 = IC, DIP package, 8 pins [chip_label=MC34063]
  Vin = female pin header, 1 pin [form="♀ (female)"]
  Rsc = Resistor [tolerance=±5% resistance=0.1 package=THT]
  C1 = Electrolytic Capacitor [capacitance=47µF package="100 mil [THT, electrolytic]"]
  Ct = Ceramic Capacitor [capacitance=470pF package="100 mil [THT, multilayer]"]
  Rpu = Resistor [tolerance=±5% resistance=100k package=THT]
  Rgd = Resistor [tolerance=±5% resistance=220 package=THT]
  D1 = Rectifier Diode [part_number=1N4148 package="300 mil [THT]"]
  Rb = Resistor [tolerance=±5% resistance=10k package=THT]
  L1 = female pin header, 2 pins [form="♀ (female)"]
  Co = Electrolytic Capacitor [capacitance=100µF package="100 mil [THT, electrolytic]"]
  Vout = female pin header, 1 pin [form="♀ (female)"]
  Q1 = MOSFET-PCHANNEL [part_number=AO3401A package=sot23-3]
  GND = female pin header, 2 pins [form="♀ (female)"]
  D2 = Rectifier Diode [part_number=1N5822 package="300 mil [THT]"]
  Z1 = Zener Diode [part_number=1N4732A breakdown_voltage=10V package="300 mil [THT]"]
  Rgc = Resistor [tolerance=±5% resistance=10 package=THT]
  Q2 = NPN-Transistor [part_number=BC337 package="TO92 [THT]"]

nets:
  N1: U1.pin1, U1.pin8, Rgd.Pin_0
  GND: U1.pin2, U1.pin4, C1.-, Ct.0, Co.-, GND.pin1, GND.pin2, D2.anode
  N2: U1.pin3, Ct.1
  N3: U1.pin5, L1.pin1, Co.+, Vout.pin1
  N4: U1.pin6, Rsc.Pin_1
  N5: U1.pin7, Rsc.Pin_0, Rpu.Pin_0, Rb.Pin_0, Q1.S, Z1.cathode, Q2.C
  18V: Vin.pin1, C1.+
  N6: Rpu.Pin_1, D1.anode, Q1.G, Z1.anode, Rgc.Pin_0
  N7: Rgd.Pin_1, D1.cathode, Rb.Pin_1, Q2.B
  N8: L1.pin2, Q1.D, D2.cathode
  N9: Rgc.Pin_1, Q2.E

notes:
  30uH
