# Fritzing sketch cc-univ (saved by Fritzing 0.9.3b)
circuit board: 8.59112cm x 5.458cm
circuit board: 8.59112cm x 5.458cm
breadboards: 1

parts:
  Rv = Trimmer Potentiometer [package=THT]
  Z1 = Zener Diode [part_number=1N4732A breakdown_voltage=5.1V package="300 mil [THT]"]
  R1 = Resistor [tolerance=±5% resistance=2.2k package=THT]
  R2 = Resistor [tolerance=±5% resistance=1k package=THT]
  Vcc = female pin header, 1 pin [form="♀ (female)"]
  GND = female pin header, 1 pin [form="♀ (female)"]
  C1 = Electrolytic Capacitor [capacitance=33µF package="100 mil [THT, electrolytic]"]
  Vref1 = female pin header, 1 pin [form="♀ (female)"]
  Vin1 = female pin header, 1 pin [form="♀ (female)"]
  Vin2 = female pin header, 1 pin [form="♀ (female)"]
  GND_2 = female pin header, 1 pin [form="♀ (female)"]
  Vref = female pin header, 1 pin [form="♀ (female)"]
  Vcc_2 = female pin header, 1 pin [form="♀ (female)"]
  Q1 = NPN-Transistor [package="TO92 [THT]"]
  Rs2 = Resistor [tolerance=±5% resistance=1 package=THT]
  Rs1 = Resistor [tolerance=±5% resistance=1 package=THT]
  Q2 = NPN-Transistor [package="TO92 [THT]"]
  Rb1 = Resistor [tolerance=±5% resistance=10k package=THT]
  Rb2 = Resistor [tolerance=±5% resistance=10k package=THT]
  U1 = LM 358 Dual Op-Amp [package="DIP8 [THT]"]

nets:
  N1: Rv.wiper, Z1.cathode, R1.Pin_1, C1.+
  N2: Rv.leg2, R2.Pin_0, Vref1.pin1
  GND: Z1.anode, R2.Pin_1, GND.pin1, C1.-
  18V: R1.Pin_0, Vcc.pin1
  N3: Vin1.pin1, Q1.C
  N4: Vin2.pin1, Q2.C
  N5: GND_2.pin1, Rs2.Pin_1, Rs1.Pin_1, U1.connector3
  N6: Vref.pin1, U1.connector2, U1.connector4
  N7: Vcc_2.pin1, U1.connector7
  N8: Q1.E, Rs1.Pin_0, U1.connector1
  N9: Q1.B, Rb1.Pin_0
  N10: Rs2.Pin_0, Q2.E, U1.connector5
  N11: Q2.B, Rb2.Pin_0
  N12: Rb1.Pin_1, U1.connector0
  N13: Rb2.Pin_1, U1.connector6

notes:
  100kΩ

custom parts:
  Trimmer Potentiometer: A standard 6mm trimmer potentiometer.
