# Fritzing sketch dimmer (saved by Fritzing 0.9.3b)
circuit board: 8.59112cm x 5.458cm
breadboards: 1

parts:
  VIN18V = female pin header, 1 pin [form="♀ (female)"]
  VIN5V = female pin header, 1 pin [form="♀ (female)"]
  GND = female pin header, 1 pin [form="♀ (female)"]
  U1 = 555 Timer [package="DIP8 [THT]"]
  R2 = Resistor [tolerance=±5% resistance=1k package=THT]
  R3 = female pin header, 3 pins [form="♀ (female)"]
  Ct = Ceramic Capacitor [capacitance=10nF package="100 mil [THT, multilayer]"]
  Re = Resistor [tolerance=±5% resistance=1k package=THT]
  Q2 = NPN-Transistor [part_number=BC337 package="TO92 [THT]"]
  Rpu = Resistor [tolerance=±5% resistance=4.7k package=THT]
  Vout = female pin header, 1 pin [form="♀ (female)"]
  GND_2 = female pin header, 1 pin [form="♀ (female)"]
  Dc = Diode [part_number=1N4148 package=diode-1n4148]
  Z1 = Zener Diode [part_number=1N4732A breakdown_voltage=10V package="300 mil [THT]"]
  Dd = Diode [part_number=1N4148 package=diode-1n4148]
  Q1 = MOSFET-PCHANNEL [part_number=AO3401A package=sot23-3]
  R1 = Resistor [tolerance=±5% resistance=10k package=THT]

nets:
  18V: VIN18V.pin1, Rpu.Pin_0, Z1.cathode, Q1.S
  5V: VIN5V.pin1, U1.Pin_4, U1.Pin_8, R1.Pin_0
  GND: GND.pin1, U1.Pin_1, U1.Pin_2, U1.Pin_6, Ct.0, Ct.1, Re.Pin_1, GND_2.pin1, Dc.C, Dd.A
  N1: U1.Pin_3, Q2.B
  N2: U1.Pin_7, R2.Pin_1, R1.Pin_1
  N3: R2.Pin_0, R3.pin2
  N4: R3.pin1, Dc.A
  N5: R3.pin3, Dd.C
  N6: Re.Pin_0, Q2.E
  N7: Q2.C, Rpu.Pin_1, Z1.anode, Q1.G
  N8: Vout.pin1, Q1.D

notes:
  100kΩ
