# Fritzing sketch power-distribution-panel (saved by Fritzing 0.9.3b)
circuit board: 8.59112cm x 5.458cm
breadboards: 1

parts:
  Vin18v = female pin header, 1 pin [form="♀ (female)"]
  Vin5v = female pin header, 1 pin [form="♀ (female)"]
  Vin1v25 = female pin header, 1 pin [form="♀ (female)"]
  SW1 = female pin header, 2 pins [form="♀ (female)"]
  Vout18v = female pin header, 1 pin [form="♀ (female)"]
  Rc1 = Resistor [tolerance=±5% resistance=10k package=THT]
  Rd1 = Resistor [tolerance=±5% resistance=10k package=THT]
  Vout5v = female pin header, 1 pin [form="♀ (female)"]
  Vout1v25 = female pin header, 1 pin [form="♀ (female)"]
  SW2 = female pin header, 2 pins [form="♀ (female)"]
  Vout18v_2 = female pin header, 1 pin [form="♀ (female)"]
  Rc2 = Resistor [tolerance=±5% resistance=10k package=THT]
  Rd2 = Resistor [tolerance=±5% resistance=10k package=THT]
  Vout5v_2 = female pin header, 1 pin [form="♀ (female)"]
  Vout1v25_2 = female pin header, 1 pin [form="♀ (female)"]
  GND = female pin header, 2 pins [form="♀ (female)"]
  GND_2 = female pin header, 1 pin [form="♀ (female)"]
  GND_3 = female pin header, 2 pins [form="♀ (female)"]
  Q1-5v = MOSFET-NCHANNEL [part_number=AO3400A package=sot23-3]
  Q1-1v25 = MOSFET-NCHANNEL [part_number=AO3400A package=sot23-3]
  Q2-1v25 = MOSFET-PCHANNEL [part_number=AO3400A package=sot23-3]
  Q2-5v = MOSFET-PCHANNEL [part_number=AO3400A package=sot23-3]

nets:
  18V: Vin18v.pin1, SW1.pin2, SW2.pin2
  5V: Vin5v.pin1, Q1-5v.D, Q2-5v.D
  1.25V: Vin1v25.pin1, Q1-1v25.D, Q2-1v25.D
  N1: SW1.pin1, Vout18v.pin1, Rc1.Pin_0
  N2: Rc1.Pin_1, Rd1.Pin_0, Q1-5v.G, Q1-1v25.G
  GND: Rd1.Pin_1, Rd2.Pin_1, GND.pin1, GND.pin2, GND_2.pin1, GND_3.pin1, GND_3.pin2
  N3: Vout5v.pin1, Q1-5v.S
  N4: Vout1v25.pin1, Q1-1v25.S
  N5: SW2.pin1, Vout18v_2.pin1, Rc2.Pin_0
  N6: Rc2.Pin_1, Rd2.Pin_0, Q2-1v25.G, Q2-5v.G
  N7: Vout5v_2.pin1, Q2-5v.S
  N8: Vout1v25_2.pin1, Q2-1v25.S
